# Fritzing sketch LED RGB (saved by Fritzing 0.9.2b)
breadboards: 1

parts:
  Parte1 = IOIO for Android
  LED1 = RGB LED (com. cathode, rgb) [package="5 mm [THT]"]
  R1 = Resistor [tolerance=±5% resistance=220 package=THT]
  R2 = Resistor [tolerance=±5% resistance=220 package=THT]
  R3 = Resistor [tolerance=±5% resistance=220 package=THT]

nets:
  N1: Parte1.PIN1, R1.Pin_0
  N2: Parte1.PIN2, R2.Pin_0
  N3: Parte1.PIN3, R3.Pin_0
  N4: Parte1.GND, LED1.common_cathode
  N5: LED1.red_anode, R3.Pin_1
  N6: LED1.green_anode, R2.Pin_1
  N7: LED1.blue_anode, R1.Pin_1
