# Fritzing sketch LED (saved by Fritzing 0.9.2b)
breadboards: 1

parts:
  Parte1 = IOIO for Android
  LED1 = RGB LED (com. cathode, rgb) [package="5 mm [THT]"]
  R1 = Resistor [tolerance=±5% resistance=220 package=THT]

nets:
  N1: Parte1.PIN1, R1.Pin_0
  N2: Parte1.GND, LED1.common_cathode
  N3: LED1.blue_anode, R1.Pin_1
