# Fritzing sketch LED+Potenciometro+FotoResistencia (saved by Fritzing 0.9.2b)
breadboards: 1

parts:
  Parte1 = IOIO for Android
  U1 = MCP41xxx [package=so08]
  LED1 = RGB LED (com. cathode, rgb) [package="5 mm [THT]"]
  R1 = Resistor [tolerance=±5% resistance=220 package=THT]
  R2 = PHOTOCELL [package=photocell-kit]
  R3 = Resistor [tolerance=±5% resistance=220 package=THT]

nets:
  N1: Parte1.PIN3, Parte1.PIN9, U1.DI
  N2: Parte1.PIN6, U1.SCK
  N3: Parte1.PIN7, U1.CS
  N4: Parte1.3.3V, R2.P$2
  5V: Parte1.5V, U1.A, U1.VCC
  GND: Parte1.GND, U1.GND, U1.B, LED1.common_cathode, R3.Pin_0
  N5: Parte1.PIN39, R2.P$1, R3.Pin_1
  N6: U1.W, R1.Pin_0
  N7: LED1.blue_anode, R1.Pin_1
