# Fritzing sketch FotoResistencia (saved by Fritzing 0.9.2b)
breadboards: 1

parts:
  Parte1 = IOIO for Android
  R2 = PHOTOCELL [package=photocell-kit]
  R3 = Resistor [tolerance=±5% resistance=220 package=THT]

nets:
  N1: Parte1.3.3V, R2.P$2
  N2: Parte1.GND, R3.Pin_0
  N3: Parte1.PIN39, R2.P$1, R3.Pin_1
